# Fritzing sketch Open_ID (saved by Fritzing 1.0.5)
breadboards: 1

parts:
  Componente1 = Arduino Uno (Rev3)
  LED1 = smd LED [color="Green (560nm)" package="0805 [SMD]"]
  LED2 = smd LED [color="Red (633nm)" package="1206 [SMD]"]
  R1 = Resistor [tolerance=±5% resistance=220 package="0805 [SMD]"]
  Componente2 = RFID-RC522-v2
  J1 = Piezo Speaker
  R2 = Resistor [tolerance=±5% resistance=220 package="0805 [SMD]"]
  Componente3 = LCD1602-I2C  # not connected
  J2 = Basic Servo  # not connected

nets:
  N1: Componente1.D8, J1.pin2
  N2: Componente1.D9_PWM, Componente2.RST
  N3: Componente1.D10_PWM/SS, Componente2.MOSI
  N4: Componente1.D11_PWM/MOSI, Componente2.SDA
  N5: Componente1.D12/MISO, Componente2.MISO
  N6: Componente1.D13/SCK, Componente2.SCK
  N7: Componente1.D6_PWM, R2.Pin_1
  3V3: Componente1.3V3, Componente2.3.3V
  N8: LED1.cathode, LED2.cathode, Componente2.GND, J1.pin1
  N9: LED1.anode, R1.Pin_0
  N10: LED2.anode, R2.Pin_0

custom parts:
  RFID-RC522-v2: A simple China made RFID-RC522 Reader; do check the pin labels, as this is a MFRC522 based clone.
  LCD1602-I2C: A standard character display, usually with 2x16 characters. Comes in many colors with LCM1602 IIC attached.
